# Fritzing sketch Pro-Social_Operant_Chambers (saved by Fritzing 0.9.3b)

parts:
  Composant1 = Arduino Uno (Rev3)
  S1 = Momentary Switch [package=ksa_sealed_tac_switch]
  J1 = Basic Servo
  J2 = Basic Servo
  J3 = Basic Servo
  J4 = Basic Servo
  R1 = Resistor [tolerance=±5% resistance=10k package="0603 [SMD]"]
  D2F1 = D2F-FL Omron Snap Action Limit Switch with Level
  D2F2 = D2F-FL Omron Snap Action Limit Switch with Level

nets:
  N1: Composant1.D12/MISO, D2F1.NC
  GND: Composant1.GND, J1.gnd, J2.gnd, J3.gnd, J4.gnd, R1.Pin_0, D2F1.COM, D2F2.COM
  N2: Composant1.D2, J3.pulse
  N3: Composant1.D3_PWM, J4.pulse
  N4: Composant1.D4, J2.pulse
  N5: Composant1.D5_PWM, J1.pulse
  N6: Composant1.D6_PWM, D2F2.NC
  N7: Composant1.D7, S1.3, R1.Pin_1
  N8: Composant1.5V, S1.1, D2F1.NO, D2F2.NO
  VCC: Composant1.VIN, J1.vcc, J2.vcc, J3.vcc, J4.vcc

custom parts:
  D2F-FL Omron Snap Action Limit Switch with Level: Snap action switch with stainless steel lever.
